// Logisim project CMSC313_Proj1.circ as structural Verilog
module A (
  input  A,
  input  B,
  input  C,
  output F
);

  wire and_1_out, and_2_out;

  not not_1 (A, B);
  and and_1 (and_1_out, A, A);
  and and_2 (and_2_out, B, C, C);
  or or_1 (F, and_1_out, and_2_out, and_2_out);
endmodule
